# Fritzing sketch main (saved by Fritzing 0.9.6b)
breadboards: 1

parts:
  PIC_16F877A1 = PIC 16F877A [package=THT]
  M1 = Stepper Motor - Bipolar

nets:
  N1: PIC_16F877A1.RB0/INT, M1.D
  N2: PIC_16F877A1.RB1, M1.B
  N3: PIC_16F877A1.RB2, M1.C
  N4: PIC_16F877A1.RB3, M1.A
